// Logisim project waitstate_ez80_esp_bus.circ as structural Verilog: 1 circuit, main circuit main
module main (
  input  in_1,
  input  in_2,
  input  ESPRDY_n,
  input  Z80RD_n,
  input  Z80WR_n,
  input  Z80CS_n,
  input  Z80D0,
  input  Z80D1,
  input  Z80D2,
  input  Z80D3,
  input  Z80D4,
  input  Z80D5,
  input  Z80D6,
  input  Z80D7,
  input  in_15,
  input  in_16,
  input  in_17,
  input  in_18,
  input  in_19,
  input  in_20,
  input  in_21,
  input  in_22,
  output Z80HALT_n,
  output ESPRD_n,
  output ESPWR_n,
  output ESPD0,
  output ESPD1,
  output ESPD2,
  output ESPD3,
  output ESPD4,
  output ESPD5,
  output ESPD6,
  output ESPD7,
  output out_34,
  output out_35,
  output out_36,
  output out_37,
  output out_38,
  output out_39,
  output out_40,
  output out_41
);

  wire n7400_1_pin6, n7474_1_pin3;

  _7432 #(.ShowInternalStructure("true")) u_7432_1 (
    .pin1(Z80WR_n), .pin2(Z80CS_n), .pin3(ESPWR_n), .pin13(Z80RD_n), .pin12(Z80CS_n), .pin11(ESPRD_n));  // open: pin4, pin5, pin6, pin10, pin9, pin8
  _7474 #(.ShowInternalStructure("true")) u_7474_1 (
    .pin1(in_1), .pin2(in_2), .pin3(n7474_1_pin3), .pin4(ESPRDY_n), .pin5(Z80HALT_n));  // open: pin6, pin13, pin12, pin11, pin10, pin9, pin8
  _7400 #(.ShowInternalStructure("true")) u_7400_1 (
    .pin1(ESPRD_n), .pin2(ESPWR_n), .pin3(n7474_1_pin3), .pin4(n7474_1_pin3), .pin5(n7474_1_pin3),
    .pin6(n7400_1_pin6));  // open: pin13, pin12, pin11, pin10, pin9, pin8
  _74245 #(.ShowInternalStructure("true")) u_74245_1 (
    .pin1(ESPRD_n), .pin2(Z80D0), .pin3(Z80D1), .pin4(Z80D2), .pin5(Z80D3), .pin6(Z80D4), .pin7(Z80D5),
    .pin8(Z80D6), .pin9(Z80D7), .pin19(n7400_1_pin6), .pin18(ESPD0), .pin17(ESPD1), .pin16(ESPD2),
    .pin15(ESPD3), .pin14(ESPD4), .pin13(ESPD5), .pin12(ESPD6), .pin11(ESPD7));
  _74245 #(.ShowInternalStructure("true")) u_74245_2 (
    .pin1(ESPRD_n), .pin2(out_34), .pin3(out_35), .pin4(out_36), .pin5(out_37), .pin6(out_38), .pin7(out_39),
    .pin8(out_40), .pin9(out_41), .pin19(n7400_1_pin6), .pin18(in_15), .pin17(in_16), .pin16(in_17),
    .pin15(in_18), .pin14(in_19), .pin13(in_20), .pin12(in_21), .pin11(in_22));

  // Notes on the sheet:
  //   Two 74245s are actually one
  //   OEn when ESPRD or ESPWR
  //   OEn when ESPRD or ESPWR
  //   HALTn reset to H when ESPRDY becomes L
endmodule
